# Fritzing sketch Fritzing Sketch with perfboard (saved by Fritzing 0.9.3b)
perfboards: 1

parts:
  Onderdeel2 = Arduino Nano (Rev3.0)  # not connected
  J3 = Power Jack [part_number="5V 1000mA input" package=power_jack_smd]  # not connected
  Q4 = NPN-Transistor [package="TO92 [THT]"]  # not connected
  Q5 = NPN-Transistor [package="TO92 [THT]"]  # not connected
  Grove2 = Grove 4 Digit Display  # not connected
  R9 = Resistor [tolerance=±5% resistance=10k package="0805 [SMD]"]  # not connected
  LED3 = smd LED [color="Green (555nm)" package="0805 [SMD]"]  # not connected
  R10 = Resistor [tolerance=±5% resistance=100 package="0805 [SMD]"]  # not connected
  R11 = Resistor [tolerance=±5% resistance=10k package="0805 [SMD]"]  # not connected
  LED4 = smd LED [color="Red (633nm)" package="0805 [SMD]"]  # not connected
  S4 = Round Pushbutton  # not connected
  R13 = Resistor [tolerance=±5% resistance=100 package="0805 [SMD]"]  # not connected
  R14 = Resistor [tolerance=±5% resistance=10k package="0805 [SMD]"]  # not connected
  ZS-042_RTC2 = ZS-042 RTC Module  # not connected
  Q6 = NPN-Transistor [package="TO92 [THT]"]  # not connected
  R15 = Resistor [tolerance=±5% resistance=10k package="0805 [SMD]"]  # not connected
  J4 = Piezo Speaker
  R16 = Rotary Potentiometer (Small) [maximum_resistance=100kΩ package=THT]
  S5 = Pushbutton [package="[THT]"]
  S6 = Pushbutton [package="[THT]"]

nets:
  N1: J4.pin2, R16.leg1
  N2: S5.Pin_3, S5.Pin_4
  N3: S6.Pin_3, S6.Pin_4
